# Fritzing sketch schema (saved by Fritzing 0.9.3b)
breadboards: 1

parts:
  Raspberry_Pi_1 = Raspberry Pi 3 [part_number=RPI-3-V1.2]
  U1 = LCD-16X2 [package=lcd-16x2_noholes]
  R1 = Rotary Potentiometer (Small) [maximum_resistance=10kΩ package=THT]

nets:
  N1: Raspberry_Pi_1.GIPO21, U1.DB7
  N2: Raspberry_Pi_1.GIPO20, U1.DB6
  N3: Raspberry_Pi_1.GIPO16, U1.DB5
  N4: Raspberry_Pi_1.GIPO12, U1.DB4
  N5: Raspberry_Pi_1.GIPO23, U1.E
  N6: Raspberry_Pi_1.GIPO18, U1.RS
  GND: Raspberry_Pi_1.GND, U1.VSS, U1.R_W, U1.K, R1.leg2
  5V: Raspberry_Pi_1.5V, U1.VDD, U1.A, R1.leg1
  N7: U1.VO, R1.wiper
