# Fritzing sketch schema1 (saved by Fritzing 0.9.3b)
breadboards: 1

parts:
  Raspberry_Pi_1 = Raspberry Pi 3 [part_number=RPI-3-V1.2]
  U1 = LCD-16X2 [package=lcd-16x2_noholes]
  R1 = Rotary Potentiometer (Small) [maximum_resistance=10kΩ package=THT]
  R2 = Resistor [tolerance=±5% resistance=4.7k package=THT]
  R3 = Photocell (LDR) [package=THT]
  C1 = Electrolytic Capacitor [capacitance=1µF package="100 mil [THT, electrolytic]"]
  Q1 = NPN-Transistor [part_number=BC546B package="TO92 [THT]"]
  KY-1 = Keyes Relay [package=THT]
  R4 = Resistor [tolerance=±5% resistance=10k package=THT]
  R5 = Resistor [tolerance=±5% resistance=10k package=THT]

nets:
  N1: Raspberry_Pi_1.GIPO21, U1.DB7
  N2: Raspberry_Pi_1.GIPO20, U1.DB6
  N3: Raspberry_Pi_1.GIPO16, U1.DB5
  N4: Raspberry_Pi_1.GIPO12, U1.DB4
  N5: Raspberry_Pi_1.GIPO25, R4.Pin_1
  N6: Raspberry_Pi_1.GIPO24, R3.pin_0, C1.+
  N7: Raspberry_Pi_1.GIPO23, U1.E
  N8: Raspberry_Pi_1.GIPO18, U1.RS
  GND: Raspberry_Pi_1.GND, U1.VSS, U1.R_W, U1.K, R1.leg2, C1.-, Q1.E, R5.Pin_0
  5V: Raspberry_Pi_1.5V, U1.VDD, U1.A, R1.leg1, R2.Pin_0, KY-1.signal, KY-1.power
  N9: U1.VO, R1.wiper
  N10: R2.Pin_1, R3.pin_1
  N11: Q1.B, R4.Pin_0, R5.Pin_1
  N12: Q1.C, KY-1.ground

notes:
  Connected to GPIO_06

custom parts:
  Keyes Relay: The Keyes 5V relay module is suitable for SCM development, home appliance control. It uses a 5V~12V TIL control signal which can control DC / AC signal.
